# Fritzing sketch cap sketch (saved by Fritzing 1.0.4)

parts:
  U1 = ESP32-38PinWide [part_number=ESP32-38PinWide]
  DHT11_1 = DHT11 module
  BAT1 = Battery Holders [package=battery-aa-kit]
  R3 = Resistor [tolerance=±5% power=0.25W resistance=1k package=THT]
  R4 = Resistor [tolerance=±5% power=0.25W resistance=1k package=THT]
  R5 = Resistor [tolerance=±5% power=0.25W resistance=47k package=THT]
  R6 = Resistor [tolerance=±5% power=0.25W resistance=1M package=THT]
  R7 = Resistor [tolerance=±5% power=0.25W resistance=1k package=THT]
  R8 = Resistor [tolerance=±5% power=0.25W resistance=68k package=THT]
  ZTP-135SR1 = ZTP-135SR
  U2 = LM358 [package=dip08]
  R9 = Resistor [tolerance=±5% resistance=8.2k package="0402 [SMD]"]
  R10 = Resistor [tolerance=±5% resistance=8.2k package="0402 [SMD]"]
  C1 = Ceramic Capacitor [capacitance=100nF voltage=35V package="200 mil [THT, multilayer]"]
  FC-1 = Sound Sensor

nets:
  N1: U1.GPIO36, R7.Pin_1, U2.G$2_OUT
  N2: U1.GPIO39, R3.Pin_0, ZTP-135SR1.pin2
  N3: U1.GPIO34, DHT11_1.DATA
  N4: U1.GPIO35, FC-1.OUT
  VCC: DHT11_1.VCC, BAT1.+, R3.Pin_1, R8.Pin_1, U2.G$1_V+, C1.0, FC-1.VCC
  GND: DHT11_1.GND, BAT1.-, ZTP-135SR1.pin4, U2.G$1_V-, R9.Pin_1, C1.1, FC-1.GND
  N5: R4.Pin_0, ZTP-135SR1.pin3
  N6: R4.Pin_1, R6.Pin_0, U2.G$1_-IN
  N7: R5.Pin_0, ZTP-135SR1.pin1
  N8: R5.Pin_1, U2.G$1_+IN
  N9: R6.Pin_1, U2.G$1_OUT, R10.Pin_1
  N10: R7.Pin_0, U2.G$2_-IN, R9.Pin_0
  N11: R8.Pin_0, U2.G$2_+IN, R10.Pin_0

notes:
  5V power source
  Circuit required for the sensor to work.
  Link: https://www.instructables.com/Thermopile-Sensor/
  sound module
  DHT 11 to measure humidity and temperature

custom parts:
  ESP32-38PinWide: Generic 38-Pin ESP32 with wide format (only access to one side of pins on a breadboard) based on Stephen Lilley's HiLetgo ESP-WROOM-32 ESP32 ESP-32S Development Board.
  DHT11 module: https://cdn-learn.adafruit.com/downloads/pdf/dht.pdf DHT11 black pcb module reference by:https://github.com/adafruit/Fritzing-Library/blob/master/parts/DHT11%20Humitidy%20and%20Temperature%20Sensor.fzpz
